# Fritzing sketch electronics (saved by Fritzing 0.9.9b)
breadboards: 1

parts:
  Servo = Basic Servo
  WeMos_D1_Mini1 = WeMos D1 Mini
  5V_@_1A_Boost_Converter = PowerBoost 500 Charger
  BatteryPack = Battery
  Switch = Taiway 100-SP-X-T1 SPDT Miniature Toggle Switch [part_number=100-SP-X-T1-0-0-B1-M2 package=THT]

nets:
  GND: Servo.gnd, WeMos_D1_Mini1.G, 5V_@_1A_Boost_Converter.GND, 5V_@_1A_Boost_Converter.USB, BatteryPack.-
  VCC: Servo.vcc, WeMos_D1_Mini1.5V, 5V_@_1A_Boost_Converter.5.0V
  N1: Servo.pulse, WeMos_D1_Mini1.D1
  N2: 5V_@_1A_Boost_Converter.VBAT_IN, Switch.L2
  N3: BatteryPack.+, Switch.COM

notes:
  I used the TPS61023 Miniboost 5V @1A. just used this since it was the closest library part.
  I used the Miniboost TPS61023 but this library part was closest and has some shared pins.
